# Fritzing sketch FreezerBuddy (saved by Fritzing 0.9.6b)
circuit board: 6.1888cm x 5.09679cm
breadboards: 1

parts:
  RELAY = RELAY-SOLIDSTATE [package=relay-s108t02]
  ARD_NANO = Arduino Nano (Rev3.0)
  HLK-PM1 = HLK-PM12 [part_number=HLK-PM12]
  COMP_AC = Camdenboss CTB0158-2 [part_number=CTB0158-2 package=THT]
  AC_IN = Camdenboss CTB0158-2 [part_number=CTB0158-2 package=THT]
  TEMP = Camdenboss CTB0158-3 [part_number=CTB0158-3 package=THT]
  DISP = Camdenboss CTB0158-4 [part_number=CTB0158-4 package=THT]
  JP1 = Header 4 [package=1x04-smd]  # not connected

nets:
  N1: RELAY.T1, COMP_AC.pin2
  N2: RELAY.T2, HLK-PM1.AC_2, AC_IN.pin1
  N3: RELAY.+, ARD_NANO.D2
  N4: RELAY.-, ARD_NANO.GND, HLK-PM1.-Vo, TEMP.pin2, DISP.pin3
  N5: ARD_NANO.D4, DISP.pin2
  N6: ARD_NANO.D5, DISP.pin1
  N7: ARD_NANO.D12/MISO, TEMP.pin3
  N8: ARD_NANO.VIN, HLK-PM1.+Vo, TEMP.pin1, DISP.pin4
  N9: HLK-PM1.AC_1, COMP_AC.pin1, AC_IN.pin2

notes:
  AC IN
  AC OUT
  +
  -
  D
  CLK
  DIO
