# Fritzing sketch freezerbuddy (saved by Fritzing 0.9.10b)
circuit board: 6.1888cm x 5.09679cm
breadboards: 1

parts:
  ARD_NANO = Arduino Nano (Rev3.0)
  DISP = male pin header, 4 pins [form="♂ (male)"]
  TEMP = male pin header, 3 pins [form="♂ (male)"]
  AC_IN = Camdenboss CTB0158-4 [part_number=CTB0158-4 package=THT]
  HLK-PM12 = HLK-PM01
  AQG1 = Panasonic Solid State Relay AQG22205 [mpn=AQG22205 part_number=AQG22205]

nets:
  N1: ARD_NANO.GND, DISP.pin4, TEMP.pin3, HLK-PM12.-Vo, AQG1.-
  N2: ARD_NANO.D2, AQG1.+
  N3: ARD_NANO.D4, DISP.pin1
  N4: ARD_NANO.D5, DISP.pin2
  N5: ARD_NANO.D10, TEMP.pin1
  N6: ARD_NANO.VIN, HLK-PM12.+Vo
  N7: ARD_NANO.5V, DISP.pin3, TEMP.pin2
  N8: AC_IN.pin1, HLK-PM12.AC#1, AQG1.T2
  N9: AC_IN.pin2, AC_IN.pin3, HLK-PM12.AC#0
  N10: AC_IN.pin4, AQG1.T1

notes:
  AC IN
  AC OUT
  +
  -
  D
  freezerbuddy v3
  CLK
  DIO

custom parts:
  Panasonic Solid State Relay AQG22205: Panasonic AQG22205 solid-state relay.
